# Fritzing sketch Tracker (saved by Fritzing 0.9.6b)
breadboards: 1

parts:
  Mod1 = Heltec WiFi LoRa 32 V2 [part_number=HTIT-WB32LA]
  E108-GN02D = GP-2106 [package=gp-2106]
  J1 = Piezo Speaker

nets:
  GND: Mod1.GND, E108-GN02D.GND, J1.pin1
  N1: Mod1.pin_20, E108-GN02D.VCC
  N2: Mod1.pin_29, J1.pin2
  N3: Mod1.pin_33, E108-GN02D.ONOFF
  N4: Mod1.pin_35, E108-GN02D.RX
  N5: Mod1.pin_36, E108-GN02D.TX
